# Fritzing sketch Cds_side (saved by Fritzing 0.9.2b)
breadboards: 1

parts:
  パーツ1 = Arduino Uno (Rev3)
  R1 = Resistor [tolerance=±5% resistance=220 package=THT]
  R2 = Photocell (LDR) [package=THT]

nets:
  N1: パーツ1.A0, R1.Pin_1, R2.pin_0
  N2: パーツ1.GND, R1.Pin_0
  N3: パーツ1.5V, R2.pin_1

notes:
  Cdsセル
  抵抗10kΩ
