# Fritzing sketch led_side (saved by Fritzing 0.9.2b)
breadboards: 1

parts:
  パーツ1 = Arduino Uno (Rev3)
  LED1 = LED - 5mm [color="Green (570nm)" package="5 mm [THT]"]
  R1 = Resistor [tolerance=±5% resistance=220 package=THT]

nets:
  N1: パーツ1.D11_PWM/MOSI, R1.Pin_1
  N2: パーツ1.GND, LED1.cathode
  N3: LED1.anode, R1.Pin_0

notes:
  高輝度LED
  抵抗100Ω
